# Fritzing sketch Temperature_Humidity_schematic (saved by Fritzing 0.9.3b)
breadboards: 1

parts:
  DHT2 = DHT11 Humitidy and Temperature Sensor (3 pins)
  Εξάρτημα1 = Arduino Nano (Rev3.0)
  R1 = Resistor [tolerance=±5% resistance=220 package="2512 [SMD]"]

nets:
  N1: DHT2.DATA, Εξάρτημα1.D2, R1.Pin_0
  VDD: DHT2.VDD, Εξάρτημα1.3V3, R1.Pin_1
  GND: DHT2.GND, Εξάρτημα1.GND

notes:
  Connect a10k Resistor between Data Pin and Power Pin of the Sensor.
  Gnd Pin (Black)
  Power Pin (Red)
  Data Pin (Yellow)

custom parts:
  DHT11 Humitidy and Temperature Sensor (3 pins): DHT11 Humidity and Temperature Sensor (3 pins) from the design created by John De Cristofaro for Adafruit Industries.
